# Fritzing sketch Campfire (saved by Fritzing 0.9.3b)
breadboards: 2

parts:
  Part1 = Arduino Uno (Rev3)
  S1 = Momentary Switch [package=ksa_sealed_tac_switch]
  R1 = Resistor [tolerance=±5% resistance=220 package=THT]
  R2 = PHOTOCELL [package=photocell]
  LED1 = RGB LED (com. cathode, rbg) [package="5 mm [THT]"]
  LED2 = RGB LED (com. cathode, rbg) [package="5 mm [THT]"]
  LED3 = RGB LED (com. cathode, rbg) [package="5 mm [THT]"]
  R3 = Resistor [tolerance=±5% resistance=220 package=THT]
  R4 = Resistor [tolerance=±5% resistance=220 package=THT]
  R5 = Resistor [tolerance=±5% resistance=220 package="2010 [SMD]"]
  R6 = Resistor [tolerance=±5% resistance=220 package="2010 [SMD]"]

nets:
  N1: Part1.A0, R2.P$1, R4.Pin_1
  N2: Part1.D8, S1.1, R1.Pin_0
  N3: Part1.D9_PWM, R5.Pin_0
  N4: Part1.D10_PWM/SS, R6.Pin_0
  N5: Part1.D11_PWM/MOSI, R3.Pin_1
  N6: Part1.GND, R1.Pin_1, LED1.common_cathode, LED2.common_cathode, LED3.common_cathode, R4.Pin_0
  N7: Part1.5V, R2.P$2
  N8: LED1.red_anode, R3.Pin_0
  N9: LED2.red_anode, R6.Pin_1
  N10: LED3.red_anode, R5.Pin_1
