# Fritzing sketch FadeLights (saved by Fritzing 0.9.3b)
breadboards: 2

parts:
  Part1 = Arduino Uno (Rev3)
  U1 = POT [package=pot_mammoth]
  R2 = Resistor [tolerance=±5% resistance=220 package=THT]
  R3 = Resistor [tolerance=±5% resistance=220 package=THT]
  R4 = Resistor [tolerance=±5% resistance=220 package=THT]
  LED1 = RGB LED (com. cathode, rbg) [package="5 mm [THT]"]
  R5 = Resistor [tolerance=±5% resistance=220 package=THT]
  R6 = Resistor [tolerance=±5% resistance=220 package=THT]
  R7 = Resistor [tolerance=±5% resistance=220 package=THT]
  R8 = Resistor [tolerance=±5% resistance=220 package=THT]
  R9 = Resistor [tolerance=±5% resistance=220 package=THT]
  R10 = Resistor [tolerance=±5% resistance=220 package=THT]
  LED2 = RGB LED (com. cathode, rbg) [package="5 mm [THT]"]
  LED3 = RGB LED (com. cathode, rbg) [package="5 mm [THT]"]
  R11 = Resistor [tolerance=±5% resistance=220 package=THT]

nets:
  N1: Part1.A0, U1.A
  N2: Part1.D9_PWM, R4.Pin_1, R7.Pin_1, R10.Pin_1
  N3: Part1.D10_PWM/SS, R3.Pin_1, R6.Pin_1, R9.Pin_1
  N4: Part1.D11_PWM/MOSI, R2.Pin_1, R5.Pin_1, R8.Pin_1
  N5: Part1.GND, U1.S, LED1.common_cathode, LED2.common_cathode, LED3.common_cathode
  N6: Part1.5V, R11.Pin_1
  N7: U1.E, R11.Pin_0
  N8: R2.Pin_0, LED1.red_anode
  N9: R3.Pin_0, LED1.blue_anode
  N10: R4.Pin_0, LED1.green_anode
  N11: R5.Pin_0, LED2.red_anode
  N12: R6.Pin_0, LED2.blue_anode
  N13: R7.Pin_0, LED2.green_anode
  N14: R8.Pin_0, LED3.red_anode
  N15: R9.Pin_0, LED3.blue_anode
  N16: R10.Pin_0, LED3.green_anode
