# Fritzing sketch LightSensing (saved by Fritzing 0.9.3b)
breadboards: 1

parts:
  Part1 = Arduino Uno (Rev3)
  LED1 = RGB LED (com. cathode, rbg) [package="5 mm [THT]"]
  R1 = PHOTOCELL [package=photocell]
  R2 = Resistor [tolerance=±5% resistance=220 package=THT]
  R3 = Resistor [tolerance=±5% resistance=220 package=THT]
  R4 = Resistor [tolerance=±5% resistance=220 package=THT]
  R5 = Resistor [tolerance=±5% resistance=220 package=THT]

nets:
  N1: Part1.A0, R1.P$1, R2.Pin_1
  N2: Part1.D9_PWM, R5.Pin_0
  N3: Part1.D10_PWM/SS, R4.Pin_0
  N4: Part1.D11_PWM/MOSI, R3.Pin_0
  N5: Part1.GND, LED1.common_cathode
  N6: Part1.5V, R1.P$2
  N7: LED1.red_anode, R3.Pin_1
  N8: LED1.blue_anode, R4.Pin_1
  N9: LED1.green_anode, R5.Pin_1
