# Fritzing sketch OneLED (saved by Fritzing 0.9.3b)
breadboards: 2

parts:
  R1 = Resistor [tolerance=±5% resistance=220 package=THT]
  Part1 = Arduino Uno (Rev3)
  U1 = POT [package=pot_mammoth]
  R2 = Resistor [tolerance=±5% resistance=220 package=THT]
  R3 = Resistor [tolerance=±5% resistance=220 package=THT]
  U2 = POT [package=pot_mammoth]
  U3 = POT [package=pot_mammoth]
  LED1 = RGB LED (com. cathode, rbg) [package="5 mm [THT]"]
  R4 = Resistor [tolerance=±5% resistance=220 package=THT]
  R5 = Resistor [tolerance=±5% resistance=220 package=THT]
  R6 = Resistor [tolerance=±5% resistance=220 package=THT]

nets:
  N1: R1.Pin_0, U1.E
  N2: R1.Pin_1, Part1.5V, R2.Pin_1, R3.Pin_1
  N3: Part1.A0, U1.A
  N4: Part1.A1, U2.A
  N5: Part1.A2, U3.A
  N6: Part1.D9_PWM, R4.Pin_0
  N7: Part1.D10_PWM/SS, R5.Pin_0
  N8: Part1.D11_PWM/MOSI, R6.Pin_0
  N9: Part1.GND, U1.S, U2.S, U3.S, LED1.common_cathode
  N10: R2.Pin_0, U3.E
  N11: R3.Pin_0, U2.E
  N12: LED1.red_anode, R4.Pin_1
  N13: LED1.blue_anode, R5.Pin_1
  N14: LED1.green_anode, R6.Pin_1
