# Fritzing sketch ServoMove (saved by Fritzing 0.9.3b)
breadboards: 1

parts:
  Part1 = Arduino Uno (Rev3)
  R1 = Resistor [tolerance=±5% resistance=220 package=THT]
  U1 = POT [package=pot_mammoth]
  J1 = Basic Servo

nets:
  N1: Part1.A0, U1.A
  N2: Part1.D8, J1.pulse
  5V: Part1.5V, R1.Pin_0, J1.vcc
  GND: Part1.GND, U1.S, J1.gnd
  N3: R1.Pin_1, U1.E
